# Fritzing sketch esc arduino (saved by Fritzing 0.9.3b)

parts:
  920KV_Motor1 = DJI 920 KV Motor
  M1 = ESC
  Part1 = Arduino Uno (Rev3) - ICSP
  R1 = Rotary Potentiometer (Large) [maximum_resistance=100kΩ package=THT]
  JACK1 = 2.1mm DC Barrel Jack  # not connected

nets:
  N1: 920KV_Motor1.w, M1.W
  N2: 920KV_Motor1.v, M1.V
  N3: 920KV_Motor1.u, M1.U
  N4: M1.DATA, Part1.D2
  GND: M1.GND, Part1.GND, R1.leg2
  N5: Part1.A0, R1.wiper
  N6: Part1.5V, R1.leg1

notes:
  ESC
  BLDC
  POWER
  100K POT

custom parts:
  DJI 920 KV Motor: DJI Brushless Outrunner 2212/920K Motor F330-550
  2.1mm DC Barrel Jack: 2.1mm DC Barrel Jack with Thru-Hole Connectors (breadboardable)
